# Fritzing sketch LegoOrrery (saved by Fritzing 1.0.4)

parts:
  Driver1 = 28BYJ-48 Driver Module [part_number=ULN2003 package=THT]
  SM1 = 28BYJ-48 Stepper Motor [part_number=28BYJ-48]
  Teensy_LC1 = Teensy-LC
  R1 = TRIMPOT [maximum_resistance=10kΩ knob_status=50% power=0.5W package=3386u]

nets:
  N1: Driver1.IN1, Teensy_LC1.A7/D21
  N2: Driver1.IN2, Teensy_LC1.A3/D17
  N3: Driver1.IN3, Teensy_LC1.A2/D16
  N4: Driver1.IN4, Teensy_LC1.D5
  N5: Driver1.GND, Teensy_LC1.AGND
  N6: Driver1.Vmotor, Teensy_LC1.Vin
  N7: Driver1.blue-pin, SM1.blue-pin
  N8: Driver1.pink-pin, SM1.pink-pin
  N9: Driver1.yellow-pin, SM1.yellow-pin
  N10: Driver1.orange-pin, SM1.orange-pin
  N11: Driver1.red-pin, SM1.red-pin
  N12: Teensy_LC1.D13, R1.CW
  N13: Teensy_LC1.A0/D14, R1.WIPER
  N14: Teensy_LC1.A1/D15, R1.CCW

notes:
  D21: ULN2003A IN1
  D17: ULN2003A IN2
  D16: ULN2003A IN3
  D5: ULN2003A IN4
  D13: Pot low side
  D15: Pot high side
  D14/A0: Pot wiper
  Teensy LC

custom parts:
  28BYJ-48 Driver Module: ULN2003 Driver Module for the 28BYJ-48 Unipolar Stepper Motor LED A - Blue wire - Bottom coil left LED B - Pink wire - Top coil left LED C - Yellow wire - Bottom coil right LED D - Orange wire - Top coil right Common rail - red Connector pins: blue - pink - yellow - orange - red Control pins - IN1 to IN4 Power pins - GND & Vmotor (5-12V) On/Off jumper (if removed, power to motor is cut).
  28BYJ-48 Stepper Motor: Unipolar Stepper Motor 28BYJ-48 Top coil - pink & orange Bottom coil - blue & yellow Common rail - red Connector pins: blue - pink - yellow - orange - red
  Teensy-LC: Teensy-LC (Low Cost) is a powerful 32 bit microcontroller board, with a rich set of hardware peripherals, at a very affordable price! Teensy-LC delivers an impressive collection of capabilities to make modern electronic projects simpler. It features an ARM Cortex-M0+ processor at 48 MHz, 62K Flash, 8K RAM, 12 bit analog input & output, hardware Serial, SPI & I2C, USB, and a total of 27 I/O pins.
